# Fritzing sketch CuttleFish_8825 (saved by Fritzing 1.0.4)
stripboards: 12

parts:
  Part1 = Arduino Mega 2560 (Rev3)
  M1 = Stepper Motor - Bipolar
  Power_plug1 = Power plug
  DRV_1 = DRV 8825 Stepper Motor Carrier, High Current [part_number="DRV 8825"]
  DRV_2 = DRV 8825 Stepper Motor Carrier, High Current [part_number="DRV 8825"]
  M2 = Stepper Motor - Bipolar
  DRV_3 = DRV 8825 Stepper Motor Carrier, High Current [part_number="DRV 8825"]
  M3 = Stepper Motor - Bipolar
  DRV_4 = DRV 8825 Stepper Motor Carrier, High Current [part_number="DRV 8825"]
  M4 = Stepper Motor - Bipolar
  CUI-enc1 = AMT103
  DRV_5 = DRV 8825 Stepper Motor Carrier, High Current [part_number="DRV 8825"]
  M6 = Stepper Motor - Bipolar
  M7 = 1 chan 5v relay module
  M8 = 1 chan 5v relay module
  Power_plug2 = Power plug
  L1 = Solenoid
  L3 = Solenoid
  L2 = Solenoid
  M9 = 1 chan 5v relay module

nets:
  N1: Part1.D21/SCL, CUI-enc1.B
  N2: Part1.D20/SDA, CUI-enc1.A
  N3: Part1.D14/TX3, M7.pin_3
  GND: Part1.GND, Power_plug1.GND, DRV_1.GROUND_ST/_MT, DRV_1.GROUND_LOG, DRV_2.GROUND_ST/_MT, DRV_2.GROUND_LOG, DRV_3.GROUND_ST/_MT, DRV_3.GROUND_LOG, DRV_4.GROUND_ST/_MT, DRV_4.GROUND_LOG, CUI-enc1.GND, DRV_5.GROUND_ST/_MT, DRV_5.GROUND_LOG, M7.pin_2, M8.pin_2, M9.pin_2
  N4: Part1.D11_PWM, DRV_2.ENABLE
  N5: Part1.D9_PWM, DRV_2.DIRECTION
  N6: Part1.D8_PWM, DRV_2.STEP
  5V: Part1.5V, DRV_1.MS2, DRV_1.RESET, DRV_1.SLEEP, DRV_2.MS2, DRV_2.RESET, DRV_2.SLEEP, DRV_3.MS2, DRV_3.RESET, DRV_3.SLEEP, DRV_4.MS2, DRV_4.RESET, DRV_4.SLEEP, CUI-enc1.5V, DRV_5.MS2, DRV_5.RESET, DRV_5.SLEEP, M7.pin_1, M8.pin_1, M9.pin_1
  N7: Part1.D2_PWM, M8.pin_3
  N8: Part1.D3_PWM, M9.pin_3
  N9: Part1.D4_PWM, DRV_1.STEP
  N10: Part1.D5_PWM, DRV_1.DIRECTION
  N11: Part1.D7_PWM, DRV_1.ENABLE
  N12: Part1.D30, DRV_3.STEP
  N13: Part1.D31, DRV_3.DIRECTION
  N14: Part1.D33, DRV_3.ENABLE
  N15: Part1.D36, DRV_5.STEP
  N16: Part1.D37, DRV_5.DIRECTION
  N17: Part1.D39, DRV_5.ENABLE
  N18: Part1.D40, DRV_4.STEP
  N19: Part1.D41, DRV_4.DIRECTION
  N20: Part1.D43, DRV_4.ENABLE
  N21: M1.A, DRV_1.OUT_2B
  N22: M1.C, DRV_1.OUT_2A
  N23: M1.B, DRV_1.OUT_1A
  N24: M1.D, DRV_1.OUT_1B
  N25: Power_plug1.VCC, DRV_1.VOLTAGE_ST/_MT, DRV_3.VOLTAGE_ST/_MT, DRV_4.VOLTAGE_ST/_MT, DRV_5.VOLTAGE_ST/_MT
  N26: DRV_2.OUT_2B, M2.A
  N27: DRV_2.OUT_2A, M2.C
  N28: DRV_2.OUT_1A, M2.B
  N29: DRV_2.OUT_1B, M2.D
  N30: DRV_3.OUT_2B, M3.A
  N31: DRV_3.OUT_2A, M3.C
  N32: DRV_3.OUT_1A, M3.B
  N33: DRV_3.OUT_1B, M3.D
  N34: DRV_4.OUT_2B, M4.A
  N35: DRV_4.OUT_2A, M4.C
  N36: DRV_4.OUT_1A, M4.B
  N37: DRV_4.OUT_1B, M4.D
  N38: DRV_5.OUT_2B, M6.A
  N39: DRV_5.OUT_2A, M6.C
  N40: DRV_5.OUT_1A, M6.B
  N41: DRV_5.OUT_1B, M6.D
  N42: M7.pin_4, L3.pin2
  N43: M7.pin_5, M8.pin_5, Power_plug2.VCC, M9.pin_5
  N44: M8.pin_4, L2.pin2
  N45: Power_plug2.GND, L1.pin1, L3.pin1, L2.pin1
  N46: L1.pin2, M9.pin_4

notes:
  Relay controlled pinch valves. Valves have their own power supply (12V 1 Amp)
  Linear Actuator (Step motor and encoder)
  Pump motors 3 and 4
  Pump motors 1 and 2
  Power Supply. 12 V; 2 Amp

custom parts:
  1 chan 5v relay module: 1 Channel 5V Relay Module Board Shield with Optocoupler Support High and Low Level Trigger for Arduino.
